# Fritzing sketch Arduino mega l298n (saved by Fritzing 0.9.2b)

parts:
  S1 = H-Bridge with L298N
  BAT1 = 18650 battery holder [package=battery-18650-kit]
  M1 = DC Motor
  M2 = DC Motor
  BAT3 = 18650 battery holder [package=battery-18650-kit]
  BAT5 = 18650 battery holder [package=battery-18650-kit]
  S2 = SPST Switch [package=r_sw_th]
  U1 = NodeMCU V3.0
  BAT6 = 18650 battery holder [package=battery-18650-kit]
  BAT4 = 18650 battery holder [package=battery-18650-kit]
  U2 = USB+SHIELD [package=usb-b-pth]  # not connected

nets:
  N1: S1.12V, S2.O
  N2: S1.GND, BAT5.-
  N3: S1.ENA, U1.D2
  N4: S1.IN1, U1.D3
  N5: S1.IN2, U1.D4
  N6: S1.IN3, U1.D6
  N7: S1.IN4, U1.D7
  N8: S1.ENB, U1.D8
  N9: S1.M1-01, M2.pin_1
  N10: S1.M1-02, M2.pin_2
  N11: S1.M2-01, M1.pin_2
  N12: S1.M2-02, M1.pin_1
  N13: BAT1.+, U1.Vin
  N14: BAT1.-, U1.GND
  N15: BAT3.+, S2.P
  N16: BAT3.-, BAT4.+
  N17: BAT5.+, BAT6.-
  N18: BAT6.+, BAT4.-

custom parts:
  H-Bridge with L298N: h-bridge
  18650 battery holder: 18650 Battery Holder
  NodeMCU V3.0: ESP8266 based NodeMCU
